# Fritzing sketch Honda_Tachometer (saved by Fritzing 0.8.0b)
breadboards: 1

parts:
  12VDC = Power plug
  Part1 = Arduino Leonardo (Rev3b)
  R1 = Rotary Potentiometer (Small)
  Honda_tachometer = DC Motor
  TIP120 = npn-Powertransistor [package="TO220 [THT]"]

nets:
  GND: 12VDC.GND, Part1.GND, R1.leg2, TIP120.emitter
  N1: 12VDC.VCC, Honda_tachometer.pin_1
  N2: Part1.5V, R1.leg1
  N3: Part1.A0, R1.wiper
  N4: Part1.D9_PWM/A9, TIP120.base
  N5: Honda_tachometer.pin_2, TIP120.collector
